# Fritzing sketch ventilator_v0p3 (saved by Fritzing 0.9.4)
circuit board: 10cm x 13cm
breadboards: 4

parts:
  U1 = ESP32S-HiLetgo [part_number=ESP32S-HiLetgo]
  Power_plug1 = Power plug
  Part2 = Adafruit 4-channel I2C-safe Bi-directional Logic Level Converter [part_number="Adafruit #757"]
  Part3 = Adafruit TCA9548A
  IC1 = Voltage Regulator [package=to220-igo]
  C1 = Capacitor Polarized [part_number=10uF package=cpol-radial-10uf-25v]
  C2 = Capacitor Polarized [part_number=100uF package=cpol-radial-100uf-25v]
  C3 = Ceramic Capacitor [capacitance=100nF package="100 mil [THT, multilayer]"]
  Part7 = SOIC-14 [chip_label="NPA Sensor" part_number=NPA-300B-001D package=SO]
  Part8 = SOIC-14 [chip_label="NPA Sensor" part_number=NPA-300B-001D package=SO]
  Part9 = SOIC-14 [chip_label="NPA Sensor" part_number=NPA-300B-001D package=SO]
  C4 = Ceramic Capacitor [capacitance=100nF package="200 mil [THT, multilayer]"]
  C5 = Ceramic Capacitor [capacitance=100nF package="200 mil [THT, multilayer]"]
  C6 = Ceramic Capacitor [capacitance=100nF package="200 mil [THT, multilayer]"]
  Q1 = Basic FET N-Channel [part_number=RFP30N06LE package="TO220 [THT]"]
  Q3 = Basic FET N-Channel [part_number=RFP30N06LE package="TO220 [THT]"]
  Q2 = Basic FET N-Channel [part_number=RFP30N06LE package="TO220 [THT]"]
  R1 = Resistor [tolerance=±5% resistance=10k package=THT]
  R3 = Resistor [tolerance=±5% resistance=10k package=THT]
  R2 = Resistor [tolerance=±5% resistance=10k package=THT]
  Part1 = 3.5in TFT 480x320 Touch + MicroSD
  Part10 = EasyDriver_v44
  SJ1 = Solder Jumper [package=sj_2s-no]
  SJ2 = Solder Jumper [package=sj_2s-no]
  J11 = screw terminal, 6 pins
  J10 = screw terminal, 4 pins
  J5 = male pin header, 4 pins [form="♂ (male)"]
  J9 = male pin header, 4 pins [form="♂ (male)"]
  J8 = male pin header, 4 pins [form="♂ (male)"]
  J7 = male pin header, 4 pins [form="♂ (male)"]
  J4 = male pin header, 4 pins [form="♂ (male)"]
  J6 = male pin header, 4 pins [form="♂ (male)"]

nets:
  3.3V: U1.3.3, Part2.LV, Part7.9, Part8.9, Part9.9, C4.0, C5.0, C6.0
  N1: U1.GPIO36, Part7.8
  N2: U1.GPIO39, Part8.8
  N3: U1.GPIO34, Part9.8
  N4: U1.GPIO32, Part10.DIR
  N5: U1.GPIO33, Part1.LCD_Y-
  N6: U1.GPIO25, Part1.LCD_X+
  N7: U1.GPIO26, Q2.gate, R3.Pin_0
  N8: U1.GPIO27, Q1.gate, R2.Pin_0
  N9: U1.GPIO14, Q3.gate, R1.Pin_0
  GND: U1.GND, Power_plug1.GND, Part2.GND, Part3.GND, IC1.GND, C1.-, C2.-, C3.0, Part7.6, Part8.6, Part9.6, C4.1, C5.1, C6.1, Q1.source, Q3.source, Q2.source, R1.Pin_1, R3.Pin_1, R2.Pin_1, Part1.GND, Part10.GND, SJ1.2, SJ2.1, J5.pin1, J9.pin1, J8.pin1, J7.pin1, J4.pin1, J6.pin1
  N10: U1.GPIO13, Part10.STEP
  5V: U1.VIN, Part2.HV, Part3.VCC, IC1.OUT, C2.+, C3.1, Part1.3-5V, Part1.+5V, J5.pin2, J9.pin2, J8.pin2, J7.pin2, J4.pin2, J6.pin2
  N11: U1.GPIO15, Part1.LCD_X-
  N12: U1.GPIO2, Part10.ENABLE
  N13: U1.GPIO4, Part1.LCD_Y+
  N14: U1.GPIO16, Part1.LCD_RST_5V
  N15: U1.GPIO17, Part1.LCD_RS_5V
  N16: U1.GPIO5, Part1.LCD_CS_5V
  N17: U1.GPIO18, Part1.LCD_WR_5V
  N18: U1.GPIO19, Part1.MISO
  N19: U1.GPIO21, Part2.A2
  N20: U1.GPIO22, Part2.A1
  N21: U1.GPIO23, Part1.MOSI
  12V: Power_plug1.VCC, IC1.IN, C1.+, Part10.V+, J11.pin1, J11.pin3, J11.pin5
  N22: Part2.B2, Part3.INPUTSDA
  N23: Part2.B1, Part3.INPUTSCL
  N24: Part3.2SDA, J9.pin3
  N25: Part3.2SCL, J9.pin4
  N26: Part3.3SDA, J8.pin3
  N27: Part3.3SCL, J8.pin4
  N28: Part3.4SDA, J7.pin3
  N29: Part3.4SCL, J7.pin4
  N30: Part3.5SDA, J4.pin3
  N31: Part3.5SCL, J4.pin4
  N32: Part3.0SDA, J5.pin3
  N33: Part3.0SCL, J5.pin4
  N34: Part3.1SDA, J6.pin3
  N35: Part3.1SCL, J6.pin4
  N36: Q1.drain, J11.pin4
  N37: Q3.drain, J11.pin2
  N38: Q2.drain, J11.pin6
  N39: Part10.OUT2A, J10.pin1
  N40: Part10.OUT2B, J10.pin2
  N41: Part10.OUT1A, J10.pin3
  N42: Part10.OUT1B, J10.pin4
  N43: Part10.MS1, SJ2.2
  N44: Part10.MS2, SJ1.1

notes:
  Solenoid Outputs
  Stepper Output
  I2C Ports
  ventilator, v0.1
  (Use flyback diodes at loads)
  1
  Hack The Lung v0.3

custom parts:
  ESP32S-HiLetgo: HiLetgo ESP-WROOM-32 ESP32 ESP-32S Development Board 2.4GHz Dual-Mode WiFi + Bluetooth Dual Cores Microcontroller The ESP32 integrated with Antenna switches, RF Balun, power amplifiers, low-noise amplifiers, filters, and management modules, and the entire solution occupies the least area of PCB. 2.4 GHz Wi-Fi plus Bluetooth dual-mode chip, with TSMC Ultra-low power consumption 40nm technology,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
  Adafruit 4-channel I2C-safe Bi-directional Logic Level Converter: Because the Arduino (and Basic Stamp) are 5V devices, and most modern sensors, displays, flash cards and modes are 3.3V-only, many makers find that they need to perform level shifting/conversion to protect the 3.3V device from 5V. We do have some other handy level shifters in the shop, from the DIP 74LVC245 to the fancy bi-directional TXB0108. However, neither of these are happy to work with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
  Adafruit TCA9548A: You just found the perfect I2C sensor, and you want to wire up two or three or more of them to your Arduino when you realize "Uh oh, this chip has a fixed I2C address, and from what I know about I2C, you cannot have two devices with the same address on the same SDA/SCL pins!" Are you out of luck? You would be, if you didn't have this ultra-cool TCA9548A 1-to-8 I2C multiplexer! Finally, a way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
  3.5in TFT 480x320 Touch + MicroSD: This TFT display is big (3.5" diagonal), bright (6 white-LED backlight) and colorful! 480x320 pixels with individual RGB pixel control. This display also has a resistive touchscreen attached to it already, so you can detect finger presses anywhere on the screen. There is a controller built into the display with RAM buffering, so that almost no work is done by the microcontroller. The display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
